// Logisim project FullAdder.circ as structural Verilog: 1 circuit, main circuit main
module main (
  input  C,
  input  A,
  input  B,
  output X2,
  output Y2,
  output X,
  output Y
);

  wire nand_1_out, nand_2_out, nand_3_out, nand_4_out, nand_5_out, nand_6_out, nor_1_out, xor_1_out,
       xor_2_out;

  xor xor_1 (xor_1_out, A, B);
  xor xor_2 (xor_2_out, A, B);
  nand nand_1 (nand_1_out, xor_1_out, C);
  nand nand_2 (nand_2_out, A, B);
  nand nand_3 (nand_3_out, xor_2_out, C);
  nand nand_4 (nand_4_out, A, B);
  nand nand_5 (nand_5_out, nand_1_out, nand_1_out);
  nand nand_6 (nand_6_out, nand_2_out, nand_2_out);
  xor xor_3 (X2, xor_1_out, C);
  nor nor_1 (nor_1_out, nand_5_out, nand_6_out);
  xor xor_4 (X, xor_2_out, C);
  nand nand_7 (Y, nand_3_out, nand_4_out);
  nor nor_2 (Y2, nor_1_out, nor_1_out);
endmodule
