// Logisim project SimpleFullAdder.circ as structural Verilog: 1 circuit, main circuit main
module main (
  input  C,
  input  A,
  input  B,
  output X,
  output Y
);

  wire nand_1_out, nand_2_out, xor_1_out;

  xor xor_1 (xor_1_out, A, B);
  nand nand_1 (nand_1_out, xor_1_out, C);
  nand nand_2 (nand_2_out, A, B);
  xor xor_2 (X, xor_1_out, C);
  nand nand_3 (Y, nand_1_out, nand_2_out);
endmodule
